# Fritzing sketch lightSensor (saved by Fritzing 0.9.3b)
breadboards: 1

parts:
  Часть1 = Arduino Uno (Rev3)
  Power_plug1 = Power plug  # not connected
  R1 = Photocell (LDR) [package=THT]
  R2 = Resistor [tolerance=±5% resistance=220 package=THT]

nets:
  N1: Часть1.A0, R2.Pin_1
  N2: Часть1.5V, R1.pin_0
  N3: Часть1.GND, R1.pin_1, R2.Pin_0

// code stored in the sketch: lightSensor.ino
const int pinPhoto = A0;
int raw = 0;

void setup() {
  Serial.begin(9600);
  pinMode( pinPhoto, INPUT );
}

void loop() {
  raw = analogRead( pinPhoto );
  Serial.println( raw );
  delay(200);
}
