# Fritzing sketch main (saved by Fritzing 0.9.3b)
breadboards: 1

parts:
  Часть1 = Arduino Uno (Rev3)
  ZS-042_RTC1 = ZS-042 RTC Module
  D1 = SOLAR-IXYS [package=solarbit-12x1]
  WeMos_D1_Mini_Relay_Shield_V1 = WeMos D1 Mini Relay Shield V2  # not connected
  WeMos_D1_Mini_Relay_Shield_V2 = WeMos D1 Mini Relay Shield V2  # not connected

nets:
  N1: Часть1.A1, D1.C
  N2: Часть1.A4/SDA, ZS-042_RTC1.SDA
  N3: Часть1.A5/SCL, ZS-042_RTC1.SCL
  GND: Часть1.GND, ZS-042_RTC1.GND, D1.A
